# Fritzing sketch Panel fotovoltaico (saved by Fritzing 0.9.4)

parts:
  LCD1 = LCD screen
  DHT1 = DHT22 Humidity and Temperature Sensor
  BLUETOOTH = Bluetooth HC-06
  PART1 = ML8511 UV Sensor Breakout [part_number=SEN-12705]
  Componente1 = Adafruit TSL2591 [part_number="Adafruit #1980"]
  ARDUINO = Arduino Uno (Rev3)
  Componente2 = ACS712 Low Current Sensor Board v12
  R2 = Resistor [tolerance=±5% resistance=2.4k package="2010 [SMD]"]
  R3 = Resistor [tolerance=±5% resistance=3.3k package="2010 [SMD]"]

nets:
  GND: LCD1.VSS, DHT1.NULL, BLUETOOTH.GND, ARDUINO.GND
  5V: LCD1.VDD, LCD1.LED+, DHT1.VDD, BLUETOOTH.VCC, ARDUINO.5V
  N1: LCD1.V0, ARDUINO.D3_PWM
  N2: LCD1.RS, ARDUINO.D7
  GND_2: LCD1.R/W, LCD1.LED-
  N3: LCD1.E, ARDUINO.D8
  N4: LCD1.DB4, ARDUINO.D9_PWM
  N5: LCD1.DB5, ARDUINO.D10_PWM/SS
  N6: LCD1.DB6, ARDUINO.D11_PWM/MOSI
  N7: LCD1.DB7, ARDUINO.D12/MISO
  N8: DHT1.DATA, ARDUINO.D4
  N9: BLUETOOTH.RXD, ARDUINO.D6_PWM
  N10: BLUETOOTH.TXD, ARDUINO.D5_PWM
  N11: PART1.OUT, ARDUINO.A3
  N12: Componente1.SDA, ARDUINO.A4/SDA
  N13: Componente1.SCL, ARDUINO.A5/SCL
  N14: ARDUINO.A0, Componente2.VO
  N15: ARDUINO.A1, R2.Pin_0, R3.Pin_1

custom parts:
  ML8511 UV Sensor Breakout: Description: The ML8511 breakout is an easy to use ultraviolet light sensor. The MP8511 UV Sensor works by outputing an analog signal in relation to the amount of UV light it detects. This breakout can be very handy in creating devices that warn the user of sunburn or detect the UV index as it relates to weather conditions. This sensor breakout can detect 280-390nm light most effectively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
  Adafruit TSL2591: When the future is dazzlingly-bright, this ultra-high-range luminosity sensor will help you measure it. The TSL2591 luminosity sensor is an advanced digital light sensor, ideal for use in a wide range of light situations. Compared to low cost CdS cells, this sensor is more precise, allowing for exact lux calculations and can be configured for different gain/timing ranges to detect light ranges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
